// Digital circuit SOAL NO 12 UTS.dig as structural Verilog
module SOAL_NO_12_UTS (
  input  X,
  input  Y,
  input  Z,
  output O
);

  wire and_1_out, and_2_out, and_3_out, not_1_out, not_2_out;

  not not_1 (not_1_out, Y);
  not not_2 (not_2_out, Z);
  and and_1 (and_1_out, X, Y, not_2_out);
  and and_2 (and_2_out, not_1_out, not_2_out);
  and and_3 (and_3_out, X, Z);
  or or_1 (O, and_1_out, and_3_out, and_2_out);

  // Notes on the sheet:
  //   MOCHAMAD FAQIH
  //   xyz' + y'z' + xz
endmodule
