// Digital circuit SOAL NO 15 UTS.dig as structural Verilog
module SOAL_NO_15_UTS (
  input  A,
  input  B,
  input  C,
  input  D,
  output O
);

  wire and_1_out, and_2_out, and_3_out, and_4_out, not_1_out, not_2_out, not_3_out, not_4_out;

  not not_1 (not_1_out, A);
  not not_2 (not_2_out, B);
  not not_3 (not_3_out, C);
  not not_4 (not_4_out, D);
  and and_1 (and_1_out, A, B, not_3_out);
  and and_2 (and_2_out, not_3_out, D);
  and and_3 (and_3_out, not_1_out, C, not_4_out);
  and and_4 (and_4_out, not_2_out, C, not_4_out);
  or or_1 (O, and_1_out, and_3_out, and_2_out, and_4_out);

  // Notes on the sheet:
  //   MOCHAMAD FAQIH
  //   abc' + c'd + a'cd' + b'cd'
endmodule
