// Digital circuit SOAL NO 6 UTS.dig as structural Verilog
module SOAL_NO_6_UTS (
  input  A,
  input  B,
  input  C,
  input  D,
  output O
);

  wire and_1_out, and_2_out, and_3_out, and_4_out, not_1_out, not_2_out, not_3_out;

  not not_1 (not_1_out, A);
  not not_2 (not_2_out, B);
  not not_3 (not_3_out, C);
  and and_1 (and_1_out, not_1_out, not_2_out, C);
  and and_2 (and_2_out, not_1_out, not_3_out, D);
  and and_3 (and_3_out, not_1_out, B, C);
  and and_4 (and_4_out, A, B, D);
  or or_1 (O, and_1_out, and_3_out, and_4_out, and_2_out);

  // Notes on the sheet:
  //   MOCHAMAD FAQIH
  //   A'B'C + A'C'D + A'BC + ABD
endmodule
